# Fritzing sketch Shed_20211009 (saved by Fritzing 0.9.6b)
breadboards: 2

parts:
  Part1 = Arduino Mega 2560 (Rev3)  # not connected
  Part2 = Memoire 1.0 - SD card log shield
  M1 = DC Motor  # not connected
  M2 = DC Motor  # not connected
  DS1 = DS18B20 1-Wire Temperature Sensor [part_number=DS18B20]
  DS2 = DS18B20 1-Wire Temperature Sensor [part_number=DS18B20]
  DS3 = DS18B20 1-Wire Temperature Sensor [part_number=DS18B20]
  DS4 = DS18B20 1-Wire Temperature Sensor [part_number=DS18B20]
  Part3 = BME280 Breakout
  R2 = Resistor [tolerance=±5% resistance=220 package="0805 [SMD]"]
  C1 = Capacitor Polarized [package=cpol-radial-100uf-25v]
  R3 = Resistor [tolerance=±5% resistance=220 package="0805 [SMD]"]
  C2 = Capacitor Polarized [package=cpol-radial-100uf-25v]
  Power_plug1 = Power plug

nets:
  N1: Part2.DIG_9, Part3.!CS
  N2: Part2.DIG_12, Part3.SDO/ADR
  N3: Part2.DIG_11, Part3.SDI/SDA
  N4: Part2.DIG_13, Part3.SCK/SCL
  VDD: Part2.+5V, DS1.VDD, DS2.VDD, DS3.VDD, DS4.VDD
  GND: Part2.GND, DS1.GND, DS2.GND, DS3.GND, DS4.GND
  N5: R2.Pin_0, C1.-, R3.Pin_0, C2.+, Power_plug1.VCC
  N6: R2.Pin_1, C1.+, R3.Pin_1, C2.-, Power_plug1.GND

notes:
  Cricket Temp Sensor
  Weather Station
  Jango Temp Sensor
  Shed Temp Sensor
  Case Fan (Bottom)
  Case Fan (Top)
  12V (12.44) and 2 amps from external power source
